// Logisim project S1-T13.circ as structural Verilog: 12 circuits, main circuit main
module main (
  output [3:0] COUNTER_DISPLAY_1,
  output [3:0] COUNTER_DISPLAY_2,
  output [3:0] COUNTER_DISPLAY_3
);

  wire CLOCK_1_out, CLOCK_2_out, CLOCK_3_out, COUNTER_mux_output, last_upcounter_1_mux_output, REFRESH_out,
       upcounter_1_mux_output;
  wire [6:0] characters_1_characters, keyboard_1_data;
  wire [7:0] bit_extender_1_out;
  wire [15:0] HASH_GENERATOR_a_2, HASH_GENERATOR_b_2, HASH_GENERATOR_c_2, HASH_GENERATOR_d_2,
       multiplexer_1_out, multiplexer_2_out, PADDING_MODULE_m0, PADDING_MODULE_m1, PADDING_MODULE_m2,
       PADDING_MODULE_m3, T1_t1, T2_t2, Ws_ARE_CREATED_USING_Ms_w0, Ws_ARE_CREATED_USING_Ms_w1,
       Ws_ARE_CREATED_USING_Ms_w2, Ws_ARE_CREATED_USING_Ms_w3, Ws_ARE_CREATED_USING_Ms_w4,
       Ws_ARE_CREATED_USING_Ms_w5, Ws_ARE_CREATED_USING_Ms_w6, Ws_ARE_CREATED_USING_Ms_w7;

  Button CLOCK_1 (.out(CLOCK_1_out));
  Keyboard #(.buflen(6)) keyboard_1 (.clk(CLOCK_1_out), .data(keyboard_1_data));  // open: re, clr, avail
  Padding PADDING_MODULE (
    .REFRESH(REFRESH_out), .MUX_OUTPUT(COUNTER_mux_output), .COUNTER(COUNTER_DISPLAY_1),
    .DATA(bit_extender_1_out), .M0(PADDING_MODULE_m0), .M1(PADDING_MODULE_m1), .M2(PADDING_MODULE_m2),
    .M3(PADDING_MODULE_m3));
  Multiplexer #(.select(4), .width(16)) multiplexer_1 (
    .in0(16'h428a), .in1(16'h7137), .in2(16'hb5c0), .in3(16'he9b5), .in4(16'h3956), .in5(16'h59f1),
    .in6(16'h923f), .in7(16'hab1c), .out(multiplexer_1_out), .sel(COUNTER_DISPLAY_2));  // open: in8, in9, in10, in11, in12, in13, in14, in15, en
  assign bit_extender_1_out = {{1{1'b0}}, keyboard_1_data};  // Bit_Extender bit_extender_1
  Ws Ws_ARE_CREATED_USING_Ms (
    .M0(PADDING_MODULE_m0), .M1(PADDING_MODULE_m1), .M2(PADDING_MODULE_m2), .M3(PADDING_MODULE_m3),
    .W0(Ws_ARE_CREATED_USING_Ms_w0), .W1(Ws_ARE_CREATED_USING_Ms_w1), .W2(Ws_ARE_CREATED_USING_Ms_w2),
    .W3(Ws_ARE_CREATED_USING_Ms_w3), .W4(Ws_ARE_CREATED_USING_Ms_w4), .W5(Ws_ARE_CREATED_USING_Ms_w5),
    .W6(Ws_ARE_CREATED_USING_Ms_w6), .W7(Ws_ARE_CREATED_USING_Ms_w7));
  T1 T1 (
    .b(HASH_GENERATOR_b_2), .c(HASH_GENERATOR_c_2), .d(HASH_GENERATOR_d_2), .K(multiplexer_1_out),
    .W(multiplexer_2_out), .T1(T1_t1));
  T2 T2 (.a(HASH_GENERATOR_a_2), .b(HASH_GENERATOR_b_2), .c(HASH_GENERATOR_c_2), .T2(T2_t2));
  Button CLOCK_2 (.out(CLOCK_2_out));
  Button REFRESH (.out(REFRESH_out));
  Upcounter COUNTER (
    .REFRESH(REFRESH_out), .CLOCK(CLOCK_1_out), .MUX_OUTPUT(COUNTER_mux_output), .COUNTER(COUNTER_DISPLAY_1));
  Hash_Generator HASH_GENERATOR (
    .a(16'h6a09), .b(16'hbb67), .c(16'h3c6e), .d(16'ha54f), .CLOCK_MUX_OUTPUT(upcounter_1_mux_output),
    .COUNTER(COUNTER_DISPLAY_2), .REFRESH(REFRESH_out), .T1(T1_t1), .T2(T2_t2), .a_2(HASH_GENERATOR_a_2),
    .b_2(HASH_GENERATOR_b_2), .c_2(HASH_GENERATOR_c_2), .d_2(HASH_GENERATOR_d_2));
  Upcounter upcounter_1 (
    .REFRESH(REFRESH_out), .CLOCK(CLOCK_2_out), .MUX_OUTPUT(upcounter_1_mux_output),
    .COUNTER(COUNTER_DISPLAY_2));
  Button CLOCK_3 (.out(CLOCK_3_out));
  Multiplexer #(.select(4), .width(16)) multiplexer_2 (
    .in0(Ws_ARE_CREATED_USING_Ms_w0), .in1(Ws_ARE_CREATED_USING_Ms_w1), .in2(Ws_ARE_CREATED_USING_Ms_w2),
    .in3(Ws_ARE_CREATED_USING_Ms_w3), .in4(Ws_ARE_CREATED_USING_Ms_w4), .in5(Ws_ARE_CREATED_USING_Ms_w5),
    .in6(Ws_ARE_CREATED_USING_Ms_w6), .in7(Ws_ARE_CREATED_USING_Ms_w7), .out(multiplexer_2_out),
    .sel(COUNTER_DISPLAY_2));  // open: in8, in9, in10, in11, in12, in13, in14, in15, en
  Last_Upcounter last_upcounter_1 (
    .REFRESH(REFRESH_out), .CLOCK(CLOCK_3_out), .MUX_OUTPUT(last_upcounter_1_mux_output),
    .COUNTER(COUNTER_DISPLAY_3));
  TTY #(.rows(2), .cols(20)) tty_1 (
    .data(characters_1_characters), .clk(last_upcounter_1_mux_output), .clr(REFRESH_out));  // open: we
  Characters characters_1 (
    .a(HASH_GENERATOR_a_2), .b(HASH_GENERATOR_b_2), .c(HASH_GENERATOR_c_2), .d(HASH_GENERATOR_d_2),
    .COUNTER(COUNTER_DISPLAY_3), .CHARACTERS(characters_1_characters));

  // Notes on the sheet:
  //   WORKING:
  //   1) CLICK REFRESH ONCE
  //   2) INPUT YOUR STRING
  //   INPUT YOUR STRING HERE!
  //   4) KEEP APPLYING CLOCK PULSE 2 TILL THE COUNTER DISPLAY 2 STOPS AT A NUMBER(STOPS AT 7)
  //   3) KEEP APPLYING CLOCK PULSE 1 TILL ALL THE CHARACTERS ARE READ FROM THE INPUT, OR JUST KEEP CLICKING THE BUTTON TILL THE COUNTER DISPLAY 1 STOPS AT A NUMBER(STOPS AT 7)
  //   5) KEEP APPLYING CLOCK PULSE 3 TILL THE COUNTER DISPLAY 3 STOPS AT A NUMBER(STOPS AT 8), OR JUST KEEP APPLYING THE CLOCK PULSE TILL YOU GET SEE 8 CHARACTERS IN THE OUTPUT SCREEN
  //   S1-T13: HASH GENERATOR
  //   A R SHARAN KUMAR, 231CS101
  //   ASHUTOSH KUMAR, 231CS113
  //   S B L PRATEEK, 231CS149
  //   WORKING WRITTEN BELOW...
  //   OUTPUT SCREEN
endmodule

module Padding (
  input  REFRESH,
  input  MUX_OUTPUT,
  input  [3:0] COUNTER,
  input  [7:0] DATA,
  output [15:0] M0,
  output [15:0] M1,
  output [15:0] M2,
  output [15:0] M3
);

  wire comparator_1_eq, comparator_2_eq, comparator_3_eq, comparator_4_eq, comparator_5_eq, comparator_6_eq,
       comparator_7_gt, comparator_8_gt, comparator_9_gt, comparator_10_gt, comparator_11_gt,
       comparator_12_gt;
  wire [2:0] bit_extender_1_out, bitadder_1_out;
  wire [7:0] demultiplexer_1_out0, demultiplexer_1_out1, demultiplexer_1_out2, demultiplexer_1_out3,
       demultiplexer_1_out4, demultiplexer_1_out5;

  Demultiplexer #(.select(3), .width(8)) demultiplexer_1 (
    .out0(demultiplexer_1_out0), .out1(demultiplexer_1_out1), .out2(demultiplexer_1_out2),
    .out3(demultiplexer_1_out3), .out4(demultiplexer_1_out4), .out5(demultiplexer_1_out5), .in(DATA),
    .sel(bit_extender_1_out));  // open: out6, out7, en
  Bit_Extender #(.in_width(4), .out_width(3)) bit_extender_1 (.in(COUNTER), .out(bit_extender_1_out));
  Comparator #(.width(3)) comparator_1 (.a(bit_extender_1_out), .b(3'b000), .eq(comparator_1_eq));  // open: gt, lt
  Comparator #(.width(3)) comparator_2 (.a(bit_extender_1_out), .b(3'b001), .eq(comparator_2_eq));  // open: gt, lt
  Comparator #(.width(3)) comparator_3 (.a(bit_extender_1_out), .b(3'b010), .eq(comparator_3_eq));  // open: gt, lt
  Comparator #(.width(3)) comparator_4 (.a(bit_extender_1_out), .b(3'b011), .eq(comparator_4_eq));  // open: gt, lt
  Comparator #(.width(3)) comparator_5 (.a(bit_extender_1_out), .b(3'b100), .eq(comparator_5_eq));  // open: gt, lt
  Comparator #(.width(3)) comparator_6 (.a(bit_extender_1_out), .b(3'b101), .eq(comparator_6_eq));  // open: gt, lt
  Register register_1 (.D(demultiplexer_1_out0), .en(comparator_1_eq), .Q(M0[15:8]), .clk(MUX_OUTPUT), .clr(REFRESH));
  Register register_2 (.D(demultiplexer_1_out1), .en(comparator_2_eq), .Q(M0[7:0]), .clk(MUX_OUTPUT), .clr(REFRESH));
  Register register_3 (.D(demultiplexer_1_out2), .en(comparator_3_eq), .Q(M1[15:8]), .clk(MUX_OUTPUT), .clr(REFRESH));
  Register register_4 (.D(demultiplexer_1_out3), .en(comparator_4_eq), .Q(M1[7:0]), .clk(MUX_OUTPUT), .clr(REFRESH));
  Register register_5 (.D(demultiplexer_1_out4), .en(comparator_5_eq), .Q(M2[15:8]), .clk(MUX_OUTPUT), .clr(REFRESH));
  Register register_6 (.D(demultiplexer_1_out5), .en(comparator_6_eq), .Q(M2[7:0]), .clk(MUX_OUTPUT), .clr(REFRESH));
  Comparator comparator_7 (.a(M0[15:8]), .b({8{1'b0}}), .gt(comparator_7_gt));  // open: eq, lt
  Comparator comparator_8 (.a(M0[7:0]), .b({8{1'b0}}), .gt(comparator_8_gt));  // open: eq, lt
  Comparator comparator_9 (.a(M1[15:8]), .b({8{1'b0}}), .gt(comparator_9_gt));  // open: eq, lt
  Comparator comparator_10 (.a(M1[7:0]), .b({8{1'b0}}), .gt(comparator_10_gt));  // open: eq, lt
  Comparator comparator_11 (.a(M2[15:8]), .b({8{1'b0}}), .gt(comparator_11_gt));  // open: eq, lt
  Comparator comparator_12 (.a(M2[7:0]), .b({8{1'b0}}), .gt(comparator_12_gt));  // open: eq, lt
  BitAdder #(.width(1)) bitadder_1 (
    .in0(comparator_7_gt), .in1(comparator_8_gt), .in2(comparator_9_gt), .in3(comparator_10_gt),
    .in4(comparator_11_gt), .in5(comparator_12_gt), .out(bitadder_1_out));
  assign M3 = {{13{1'b0}}, bitadder_1_out};  // Bit_Extender bit_extender_2
endmodule

module Upcounter (
  input  REFRESH,
  input  CLOCK,
  output MUX_OUTPUT,
  output [3:0] COUNTER
);

  wire and_1_out, comparator_1_eq;

  buf and_1 (and_1_out, CLOCK);  // AND_Gate
  Multiplexer multiplexer_1 (.in0(and_1_out), .in1(REFRESH), .out(MUX_OUTPUT), .sel(comparator_1_eq));  // open: en
  Counter #(.width(4), .max('hf)) counter_1 (
    .Q(COUNTER), .clk(MUX_OUTPUT), .clr(REFRESH));  // open: load, D, count, carry
  Comparator #(.width(4)) comparator_1 (.a(COUNTER), .b(4'b0111), .eq(comparator_1_eq));  // open: gt, lt
endmodule

module Ws (
  input  [15:0] M0,
  input  [15:0] M1,
  input  [15:0] M2,
  input  [15:0] M3,
  output [15:0] W0,
  output [15:0] W1,
  output [15:0] W2,
  output [15:0] W3,
  output [15:0] W4,
  output [15:0] W5,
  output [15:0] W6,
  output [15:0] W7
);

  wire [15:0] SMALL_SIGMA_FUNCTION_2_out_2, SMALL_SIGMA_FUNCTION_3_out_2, SMALL_SIGMA_FUNCTION_4_out_2,
       SMALL_SIGMA_FUNCTION_out_2;

  Small_Sigma_Function SMALL_SIGMA_FUNCTION (.in_1(M1), .out_2(SMALL_SIGMA_FUNCTION_out_2));
  Small_Sigma_Function SMALL_SIGMA_FUNCTION_2 (.in_1(M2), .out_2(SMALL_SIGMA_FUNCTION_2_out_2));
  Small_Sigma_Function SMALL_SIGMA_FUNCTION_3 (.in_1(M3), .out_2(SMALL_SIGMA_FUNCTION_3_out_2));
  Small_Sigma_Function SMALL_SIGMA_FUNCTION_4 (.in_1(W4), .out_2(SMALL_SIGMA_FUNCTION_4_out_2));
  Adder #(.width(16)) adder_1 (.a(M3), .b(SMALL_SIGMA_FUNCTION_out_2), .out(W4));  // open: cin, cout
  Adder #(.width(16)) adder_2 (.a(W4), .b(SMALL_SIGMA_FUNCTION_2_out_2), .out(W5));  // open: cin, cout
  Adder #(.width(16)) adder_3 (.a(W5), .b(SMALL_SIGMA_FUNCTION_3_out_2), .out(W6));  // open: cin, cout
  Adder #(.width(16)) adder_4 (.a(W6), .b(SMALL_SIGMA_FUNCTION_4_out_2), .out(W7));  // open: cin, cout

  assign W0 = M0;
  assign W1 = M1;
  assign W2 = M2;
  assign W3 = M3;
endmodule

module Small_Sigma_Function (
  input  [15:0] in_1,
  output [15:0] out_2
);

  wire [15:0] shifter_1_out, shifter_2_out, shifter_3_out;

  Shifter #(.width(16), .shift("rl")) shifter_1 (.in(in_1), .\dist (4'b1011), .out(shifter_1_out));
  Shifter #(.width(16), .shift("rl")) shifter_2 (.in(in_1), .\dist (4'b0111), .out(shifter_2_out));
  Shifter #(.width(16), .shift("lr")) shifter_3 (.in(in_1), .\dist (4'b0011), .out(shifter_3_out));
  ExactlyOne xor_1[15:0] (.out(out_2), .in0(shifter_1_out), .in1(shifter_2_out), .in2(shifter_3_out));
endmodule

module Hash_Generator (
  input  CLOCK_MUX_OUTPUT,
  input  [3:0] COUNTER,
  input  REFRESH,
  input  [15:0] a,
  input  [15:0] b,
  input  [15:0] c,
  input  [15:0] d,
  input  [15:0] T1,
  input  [15:0] T2,
  output [15:0] a_2,
  output [15:0] b_2,
  output [15:0] c_2,
  output [15:0] d_2
);

  wire comparator_1_eq, comparator_2_eq, comparator_3_eq, comparator_4_eq;
  wire [15:0] adder_1_out, adder_2_out, multiplexer_1_out, multiplexer_2_out, multiplexer_3_out,
       multiplexer_4_out;

  Comparator #(.width(4)) comparator_1 (.a(COUNTER), .b(4'b0000), .eq(comparator_1_eq));  // open: gt, lt
  Comparator #(.width(4)) comparator_2 (.a(COUNTER), .b(4'b0000), .eq(comparator_2_eq));  // open: gt, lt
  Comparator #(.width(4)) comparator_3 (.a(COUNTER), .b(4'b0000), .eq(comparator_3_eq));  // open: gt, lt
  Comparator #(.width(4)) comparator_4 (.a(COUNTER), .b(4'b0000), .eq(comparator_4_eq));  // open: gt, lt
  Multiplexer #(.width(16), .enable("false")) multiplexer_1 (
    .in0(a_2), .in1(a), .out(multiplexer_1_out), .sel(comparator_1_eq));
  Multiplexer #(.width(16), .enable("false")) multiplexer_2 (
    .in0(b_2), .in1(b), .out(multiplexer_2_out), .sel(comparator_2_eq));
  Multiplexer #(.width(16), .enable("false")) multiplexer_3 (
    .in0(c_2), .in1(c), .out(multiplexer_3_out), .sel(comparator_3_eq));
  Multiplexer #(.width(16), .enable("false")) multiplexer_4 (
    .in0(d_2), .in1(d), .out(multiplexer_4_out), .sel(comparator_4_eq));
  Adder #(.width(16)) adder_1 (.a(T1), .b(T2), .out(adder_1_out));  // open: cin, cout
  Adder #(.width(16)) adder_2 (.a(multiplexer_2_out), .b(T1), .out(adder_2_out));  // open: cin, cout
  Register #(.width(16)) register_1 (.D(adder_1_out), .Q(a_2), .clk(CLOCK_MUX_OUTPUT), .clr(REFRESH));  // open: en
  Register #(.width(16)) register_2 (
    .D(multiplexer_1_out), .Q(b_2), .clk(CLOCK_MUX_OUTPUT), .clr(REFRESH));  // open: en
  Register #(.width(16)) register_3 (.D(adder_2_out), .Q(c_2), .clk(CLOCK_MUX_OUTPUT), .clr(REFRESH));  // open: en
  Register #(.width(16)) register_4 (
    .D(multiplexer_3_out), .Q(d_2), .clk(CLOCK_MUX_OUTPUT), .clr(REFRESH));  // open: en
endmodule

module Sigma_1 (
  input  [15:0] c,
  output [15:0] SIGMA_1
);

  wire [15:0] shifter_1_out, shifter_2_out;

  Shifter #(.width(16), .shift("rl")) shifter_1 (.in(c), .\dist (4'b0010), .out(shifter_1_out));
  Shifter #(.width(16), .shift("rl")) shifter_2 (.in(c), .\dist (4'b0111), .out(shifter_2_out));
  Adder #(.width(16)) adder_1 (.a(shifter_1_out), .b(shifter_2_out), .out(SIGMA_1));  // open: cin, cout
endmodule

module Sigma_0 (
  input  [15:0] a,
  output [15:0] SIGMA_0
);

  wire [15:0] shifter_1_out, shifter_2_out;

  Shifter #(.width(16), .shift("rl")) shifter_1 (.in(a), .\dist (4'b0101), .out(shifter_1_out));
  Shifter #(.width(16), .shift("rl")) shifter_2 (.in(a), .\dist (4'b1011), .out(shifter_2_out));
  Adder #(.width(16)) adder_1 (.a(shifter_1_out), .b(shifter_2_out), .out(SIGMA_0));  // open: cin, cout
endmodule

module T1 (
  input  [15:0] b,
  input  [15:0] c,
  input  [15:0] d,
  input  [15:0] K,
  input  [15:0] W,
  output [15:0] T1
);

  wire [15:0] and_1_out, and_2_out, and_3_out, not_1_out, or_1_out, SIGMA1_sigma_1, xor_1_out;

  assign not_1_out = ~b;  // NOT_Gate not_1, 16 bits wide
  Sigma_1 SIGMA1 (.c(c), .SIGMA_1(SIGMA1_sigma_1));
  assign and_1_out = b & c;  // AND_Gate and_1, 16 bits wide
  assign and_2_out = d & not_1_out;  // AND_Gate and_2, 16 bits wide
  assign or_1_out = and_1_out | and_2_out;  // OR_Gate or_1, 16 bits wide
  assign and_3_out = K & d;  // AND_Gate and_3, 16 bits wide
  assign xor_1_out = SIGMA1_sigma_1 ^ or_1_out;  // XOR_Gate xor_1, 16 bits wide
  ExactlyOne xor_2[15:0] (.out(T1), .in0(xor_1_out), .in1(and_3_out), .in2(W));

  // Notes on the sheet:
  //   CHOOSE(b,c,d)
endmodule

module T2 (
  input  [15:0] a,
  input  [15:0] b,
  input  [15:0] c,
  output [15:0] T2
);

  wire [15:0] and_1_out, and_2_out, and_3_out, SIGMA0_sigma_0;

  Sigma_0 SIGMA0 (.a(a), .SIGMA_0(SIGMA0_sigma_0));
  assign and_1_out = a & b;  // AND_Gate and_1, 16 bits wide
  assign and_2_out = a & c;  // AND_Gate and_2, 16 bits wide
  assign and_3_out = b & c;  // AND_Gate and_3, 16 bits wide
  assign T2 = SIGMA0_sigma_0 | and_1_out | and_2_out | and_3_out;  // OR_Gate or_1, 16 bits wide
endmodule

module Characters (
  input  [15:0] a,
  input  [15:0] b,
  input  [15:0] c,
  input  [15:0] d,
  input  [3:0] COUNTER,
  output [6:0] CHARACTERS
);

  wire comparator_1_eq, comparator_2_lt;
  wire [7:0] adder_1_out, multiplexer_2_out, multiplexer_3_out, subtractor_1_out;
  wire [7:7] multiplexer_1_out;

  Comparator comparator_1 (.a(multiplexer_3_out), .b(8'h7f), .eq(comparator_1_eq));  // open: gt, lt
  Subtractor subtractor_1 (.a(multiplexer_3_out), .b(8'h19), .out(subtractor_1_out));  // open: bin, bout
  Multiplexer #(.width(8), .enable("false")) multiplexer_1 (
    .in0(multiplexer_3_out), .in1(subtractor_1_out), .out({multiplexer_1_out[7], CHARACTERS}),
    .sel(comparator_1_eq));
  Multiplexer #(.select(4), .width(8)) multiplexer_2 (
    .in0(a[15:8]), .in1(a[7:0]), .in2(b[15:8]), .in3(b[7:0]), .in4(c[15:8]), .in5(c[7:0]), .in6(d[15:8]),
    .in7(d[7:0]), .out(multiplexer_2_out), .sel(COUNTER));  // open: in8, in9, in10, in11, in12, in13, in14, in15, en
  Comparator comparator_2 (.a({1'b0, multiplexer_2_out[6:0]}), .b(8'h21), .lt(comparator_2_lt));  // open: gt, eq
  Adder adder_1 (.a({1'b0, multiplexer_2_out[6:0]}), .b(8'h5a), .out(adder_1_out));  // open: cin, cout
  Multiplexer #(.width(8), .enable("false")) multiplexer_3 (
    .in0({1'b0, multiplexer_2_out[6:0]}), .in1(adder_1_out), .out(multiplexer_3_out), .sel(comparator_2_lt));
endmodule

module Last_Upcounter (
  input  REFRESH,
  input  CLOCK,
  output MUX_OUTPUT,
  output [3:0] COUNTER
);

  wire and_1_out, comparator_1_eq;

  buf and_1 (and_1_out, CLOCK);  // AND_Gate
  Multiplexer multiplexer_1 (.in0(and_1_out), .in1(REFRESH), .out(MUX_OUTPUT), .sel(comparator_1_eq));  // open: en
  Counter #(.width(4), .max('hf)) counter_1 (
    .Q(COUNTER), .clk(MUX_OUTPUT), .clr(REFRESH));  // open: load, D, count, carry
  Comparator #(.width(4)) comparator_1 (.a(COUNTER), .b(4'b1000), .eq(comparator_1_eq));  // open: gt, lt
endmodule
